# Fritzing sketch Project 3 (saved by Fritzing 0.9.3b)
breadboards: 1

parts:
  Raspberry_Pi_1 = Raspberry Pi 3 [part_number=RPI-3-V1.2]
  S1 = Pushbutton [package="[THT]"]
  M1 = DC Motor
  S2 = H-Bridge with L298N
  BATT1 = 4xAA Switchable Battery Pack w/Bare Wire

nets:
  N1: Raspberry_Pi_1.3v3, S1.Pin_3, S1.Pin_4
  N2: Raspberry_Pi_1.GIPO17, S2.IN1
  N3: Raspberry_Pi_1.GIPO27, S1.Pin_1, S1.Pin_2
  GND: Raspberry_Pi_1.GND, S2.GND, BATT1.NEG
  N4: M1.pin_1, S2.M2-02
  N5: M1.pin_2, S2.M2-01
  N6: S2.12V, BATT1.POS

custom parts:
  H-Bridge with L298N: h-bridge
  4xAA Switchable Battery Pack w/Bare Wire: 4xAA Switchable Battery Pack with Bare Wire connection
